// Logisim project CPU.circ as structural Verilog: 1 circuit, main circuit main
module main (
);

  wire and_1_out, and_2_out, and_3_out, and_4_out, and_5_out, and_6_out, and_7_out, and_8_out, and_9_out,
       and_10_out, and_11_out, and_12_out, and_13_out, and_14_out, and_15_out, and_16_out, and_17_out,
       and_18_out, and_19_out, and_20_out, and_21_out, and_22_out, and_23_out, and_24_out, and_25_out,
       and_26_out, and_27_out, and_28_out, and_29_out, and_30_out, and_31_out, and_32_out, clock_1_out,
       controlled_buffer_21_out, controlled_buffer_22_out, controlled_buffer_23_out,
       controlled_buffer_24_out, controlled_buffer_25_out, controlled_buffer_26_out,
       controlled_buffer_27_out, controlled_buffer_28_out, controlled_buffer_29_out,
       controlled_buffer_30_out, controlled_buffer_31_out, controlled_buffer_32_out,
       controlled_buffer_65_out, controlled_buffer_81_out, controlled_buffer_82_out,
       controlled_buffer_84_out, controlled_buffer_86_out, controlled_buffer_87_out,
       controlled_buffer_88_out, controlled_buffer_93_out, controlled_buffer_96_out,
       controlled_buffer_100_out, controlled_buffer_102_out, controlled_buffer_105_out,
       controlled_buffer_107_out, controlled_buffer_110_out, controlled_buffer_112_out,
       controlled_buffer_114_out, controlled_buffer_116_out, controlled_buffer_118_out,
       controlled_buffer_119_out, controlled_buffer_122_out, controlled_buffer_124_out,
       controlled_buffer_126_out, controlled_buffer_128_out, controlled_buffer_130_out,
       controlled_buffer_131_out, controlled_buffer_132_out, controlled_buffer_134_out,
       controlled_buffer_136_out, controlled_buffer_138_out, controlled_buffer_140_out,
       controlled_buffer_141_out, controlled_buffer_144_out, controlled_buffer_146_out,
       controlled_buffer_148_out, controlled_buffer_150_out, controlled_buffer_151_out,
       controlled_buffer_153_out, controlled_buffer_155_out, controlled_buffer_157_out,
       controlled_buffer_159_out, controlled_buffer_161_out, controlled_buffer_163_out,
       controlled_buffer_165_out, controlled_buffer_167_out, controlled_buffer_169_out,
       controlled_buffer_171_out, controlled_buffer_173_out, controlled_buffer_175_out,
       controlled_buffer_176_out, controlled_buffer_179_out, controlled_buffer_197_out,
       controlled_buffer_199_out, controlled_buffer_200_out, controlled_buffer_206_out,
       controlled_buffer_209_out, controlled_buffer_210_out, controlled_buffer_216_out,
       controlled_buffer_218_out, controlled_buffer_221_out, controlled_buffer_224_out,
       controlled_buffer_225_out, controlled_buffer_231_out, controlled_buffer_234_out,
       controlled_buffer_237_out, d_ff_1_q, d_ff_2_q, d_ff_3_q, d_ff_4_q, d_ff_5_q, d_ff_6_q, d_ff_7_q,
       d_ff_8_q, d_ff_9_q, d_ff_10_q, d_ff_11_q, d_ff_12_q, d_ff_13_q, d_ff_14_q, d_ff_15_q, d_ff_16_q,
       d_ff_17_q, d_ff_18_q, d_ff_19_q, d_ff_20_q, d_ff_20_qn, d_ff_21_q, d_ff_21_qn, d_ff_22_qn, d_ff_23_q,
       d_ff_24_q, d_ff_24_qn, d_ff_25_qn, d_ff_26_q, d_ff_27_q, d_ff_28_q, d_ff_29_q, d_ff_30_qn, d_ff_33_qn,
       d_ff_35_qn, d_ff_37_qn, d_ff_38_qn, d_ff_39_qn, d_ff_40_qn, d_ff_41_qn, d_ff_42_q, d_ff_43_q,
       d_ff_44_q, d_ff_45_q, d_ff_45_qn, d_ff_46_q, d_ff_47_q, d_ff_47_qn, d_ff_48_q, d_ff_49_q, d_ff_50_q,
       d_ff_50_qn, d_ff_51_q, d_ff_52_q, d_ff_52_qn, decoder_1_out0, decoder_1_out1, decoder_1_out2,
       decoder_1_out3, decoder_2_out0, decoder_2_out1, decoder_2_out2, decoder_2_out3, decoder_3_out0,
       decoder_3_out1, decoder_3_out2, decoder_3_out3, decoder_4_out0, decoder_4_out1, decoder_4_out2,
       decoder_4_out3, decoder_5_out0, decoder_5_out1, decoder_5_out2, decoder_5_out3, decoder_6_out1,
       decoder_6_out2, decoder_6_out3, decoder_6_out4, decoder_6_out5, decoder_6_out6, decoder_6_out7,
       decoder_6_out8, decoder_6_out9, decoder_6_out10, decoder_6_out11, decoder_6_out12, decoder_6_out13,
       decoder_6_out14, decoder_6_out15, nor_1_out, nor_2_out, nor_3_out, nor_4_out, nor_5_out, nor_6_out,
       not_1_out, not_2_out, not_3_out, not_4_out, not_5_out, not_6_out, not_7_out, not_8_out, not_9_out,
       not_10_out, not_11_out, not_12_out, not_13_out, not_14_out, not_15_out, not_16_out, not_17_out,
       not_18_out, not_19_out, not_20_out, not_21_out, not_22_out, not_23_out, not_24_out, not_25_out,
       not_26_out, or_1_out, or_2_out, or_3_out, or_4_out, or_5_out, or_6_out, or_7_out, or_8_out, or_9_out,
       or_10_out, or_11_out, or_12_out, or_13_out, or_14_out, or_15_out, or_16_out, por_1_out,
       pull_resistor_1_node, pull_resistor_2_node, pull_resistor_3_node, pull_resistor_4_node,
       pull_resistor_5_node, pull_resistor_6_node, pull_resistor_7_node, pull_resistor_8_node,
       pull_resistor_9_node, pull_resistor_10_node, pull_resistor_11_node, pull_resistor_12_node,
       pull_resistor_13_node, pull_resistor_14_node, pull_resistor_15_node, pull_resistor_16_node,
       pull_resistor_17_node, pull_resistor_18_node, pull_resistor_19_node, pull_resistor_20_node,
       pull_resistor_25_node, pull_resistor_26_node, pull_resistor_27_node, pull_resistor_28_node,
       pull_resistor_29_node, pull_resistor_33_node, pull_resistor_34_node, pull_resistor_38_node,
       pull_resistor_48_node, pull_resistor_49_node, pull_resistor_51_node, pull_resistor_52_node,
       pull_resistor_56_node, pull_resistor_57_node, pull_resistor_58_node, pull_resistor_59_node,
       pull_resistor_61_node, pull_resistor_62_node, pull_resistor_63_node, pull_resistor_64_node,
       pull_resistor_65_node, pull_resistor_66_node, pull_resistor_67_node, pull_resistor_72_node,
       pull_resistor_80_node, pull_resistor_81_node, pull_resistor_82_node, pull_resistor_83_node,
       pull_resistor_84_node, pull_resistor_85_node, pull_resistor_86_node, pull_resistor_87_node,
       pull_resistor_88_node, pull_resistor_89_node, pull_resistor_90_node, pull_resistor_91_node,
       pull_resistor_94_node, pull_resistor_107_node, xor_1_out, xor_2_out, xor_3_out, xor_4_out, xor_5_out,
       xor_6_out, xor_7_out, xor_8_out, xor_9_out, xor_10_out, xor_11_out, xor_12_out;
  wire [1:0] d_ff_22_q, pull_resistor_30_node, pull_resistor_31_node, pull_resistor_32_node,
       pull_resistor_47_node;
  wire [3:0] d_ff_31_q;
  wire [7:0] d_ff_30_q, rom_1_data;

  Decoder #(.select(2)) decoder_1 (
    .out0(decoder_1_out0), .out1(decoder_1_out1), .out2(decoder_1_out2), .out3(decoder_1_out3),
    .sel(pull_resistor_31_node));  // open: en
  Pull_Resistor pull_resistor_1 (.node(pull_resistor_1_node));
  Pull_Resistor pull_resistor_2 (.node(pull_resistor_2_node));
  assign pull_resistor_2_node = or_1_out ? decoder_1_out1 : 1'bz;  // Controlled_Buffer controlled_buffer_1
  assign pull_resistor_1_node = or_1_out ? decoder_1_out0 : 1'bz;  // Controlled_Buffer controlled_buffer_2
  Pull_Resistor pull_resistor_3 (.node(pull_resistor_3_node));
  Pull_Resistor pull_resistor_4 (.node(pull_resistor_4_node));
  assign pull_resistor_4_node = or_1_out ? decoder_1_out3 : 1'bz;  // Controlled_Buffer controlled_buffer_3
  assign pull_resistor_3_node = or_1_out ? decoder_1_out2 : 1'bz;  // Controlled_Buffer controlled_buffer_4
  Pull_Resistor pull_resistor_5 (.node(pull_resistor_5_node));
  assign pull_resistor_5_node = pull_resistor_1_node ? controlled_buffer_88_out : 1'bz;  // Controlled_Buffer controlled_buffer_5
  Pull_Resistor pull_resistor_6 (.node(pull_resistor_6_node));
  assign pull_resistor_6_node = pull_resistor_1_node ? controlled_buffer_87_out : 1'bz;  // Controlled_Buffer controlled_buffer_6
  Pull_Resistor pull_resistor_7 (.node(pull_resistor_7_node));
  assign pull_resistor_7_node = pull_resistor_1_node ? controlled_buffer_86_out : 1'bz;  // Controlled_Buffer controlled_buffer_7
  Pull_Resistor pull_resistor_8 (.node(pull_resistor_8_node));
  assign pull_resistor_8_node = pull_resistor_1_node ? controlled_buffer_84_out : 1'bz;  // Controlled_Buffer controlled_buffer_8
  Pull_Resistor pull_resistor_9 (.node(pull_resistor_9_node));
  assign pull_resistor_9_node = pull_resistor_2_node ? controlled_buffer_88_out : 1'bz;  // Controlled_Buffer controlled_buffer_9
  Pull_Resistor pull_resistor_10 (.node(pull_resistor_10_node));
  assign pull_resistor_10_node = pull_resistor_2_node ? controlled_buffer_87_out : 1'bz;  // Controlled_Buffer controlled_buffer_10
  Pull_Resistor pull_resistor_11 (.node(pull_resistor_11_node));
  assign pull_resistor_11_node = pull_resistor_2_node ? controlled_buffer_86_out : 1'bz;  // Controlled_Buffer controlled_buffer_11
  Pull_Resistor pull_resistor_12 (.node(pull_resistor_12_node));
  assign pull_resistor_12_node = pull_resistor_2_node ? controlled_buffer_84_out : 1'bz;  // Controlled_Buffer controlled_buffer_12
  Pull_Resistor pull_resistor_13 (.node(pull_resistor_13_node));
  assign pull_resistor_13_node = pull_resistor_3_node ? controlled_buffer_88_out : 1'bz;  // Controlled_Buffer controlled_buffer_13
  Pull_Resistor pull_resistor_14 (.node(pull_resistor_14_node));
  assign pull_resistor_14_node = pull_resistor_3_node ? controlled_buffer_87_out : 1'bz;  // Controlled_Buffer controlled_buffer_14
  Pull_Resistor pull_resistor_15 (.node(pull_resistor_15_node));
  assign pull_resistor_15_node = pull_resistor_3_node ? controlled_buffer_86_out : 1'bz;  // Controlled_Buffer controlled_buffer_15
  Pull_Resistor pull_resistor_16 (.node(pull_resistor_16_node));
  assign pull_resistor_16_node = pull_resistor_3_node ? controlled_buffer_84_out : 1'bz;  // Controlled_Buffer controlled_buffer_16
  Pull_Resistor pull_resistor_17 (.node(pull_resistor_17_node));
  assign pull_resistor_17_node = pull_resistor_4_node ? controlled_buffer_88_out : 1'bz;  // Controlled_Buffer controlled_buffer_17
  Pull_Resistor pull_resistor_18 (.node(pull_resistor_18_node));
  assign pull_resistor_18_node = pull_resistor_4_node ? controlled_buffer_87_out : 1'bz;  // Controlled_Buffer controlled_buffer_18
  Pull_Resistor pull_resistor_19 (.node(pull_resistor_19_node));
  assign pull_resistor_19_node = pull_resistor_4_node ? controlled_buffer_86_out : 1'bz;  // Controlled_Buffer controlled_buffer_19
  Pull_Resistor pull_resistor_20 (.node(pull_resistor_20_node));
  assign pull_resistor_20_node = pull_resistor_4_node ? controlled_buffer_84_out : 1'bz;  // Controlled_Buffer controlled_buffer_20
  and and_1 (and_1_out, d_ff_21_q, decoder_5_out3);
  D_Flip_Flop d_ff_1 (
    .D(pull_resistor_5_node), .clk(controlled_buffer_21_out), .Q(d_ff_1_q));  // open: Qn, preset, reset
  assign controlled_buffer_21_out = pull_resistor_1_node ? and_1_out : 1'bz;  // Controlled_Buffer controlled_buffer_21
  D_Flip_Flop d_ff_2 (
    .D(pull_resistor_6_node), .clk(controlled_buffer_21_out), .Q(d_ff_2_q));  // open: Qn, preset, reset
  D_Flip_Flop d_ff_3 (
    .D(pull_resistor_7_node), .clk(controlled_buffer_21_out), .Q(d_ff_3_q));  // open: Qn, preset, reset
  D_Flip_Flop d_ff_4 (
    .D(pull_resistor_8_node), .clk(controlled_buffer_21_out), .Q(d_ff_4_q));  // open: Qn, preset, reset
  Pull_Resistor pull_resistor_21 (.node(controlled_buffer_21_out));
  D_Flip_Flop d_ff_5 (
    .D(pull_resistor_9_node), .clk(controlled_buffer_22_out), .Q(d_ff_5_q));  // open: Qn, preset, reset
  assign controlled_buffer_22_out = pull_resistor_2_node ? and_1_out : 1'bz;  // Controlled_Buffer controlled_buffer_22
  D_Flip_Flop d_ff_6 (
    .D(pull_resistor_10_node), .clk(controlled_buffer_22_out), .Q(d_ff_6_q));  // open: Qn, preset, reset
  D_Flip_Flop d_ff_7 (
    .D(pull_resistor_11_node), .clk(controlled_buffer_22_out), .Q(d_ff_7_q));  // open: Qn, preset, reset
  D_Flip_Flop d_ff_8 (
    .D(pull_resistor_12_node), .clk(controlled_buffer_22_out), .Q(d_ff_8_q));  // open: Qn, preset, reset
  Pull_Resistor pull_resistor_22 (.node(controlled_buffer_22_out));
  D_Flip_Flop d_ff_9 (
    .D(pull_resistor_13_node), .clk(controlled_buffer_23_out), .Q(d_ff_9_q));  // open: Qn, preset, reset
  assign controlled_buffer_23_out = pull_resistor_3_node ? and_1_out : 1'bz;  // Controlled_Buffer controlled_buffer_23
  D_Flip_Flop d_ff_10 (
    .D(pull_resistor_14_node), .clk(controlled_buffer_23_out), .Q(d_ff_10_q));  // open: Qn, preset, reset
  D_Flip_Flop d_ff_11 (
    .D(pull_resistor_15_node), .clk(controlled_buffer_23_out), .Q(d_ff_11_q));  // open: Qn, preset, reset
  D_Flip_Flop d_ff_12 (
    .D(pull_resistor_16_node), .clk(controlled_buffer_23_out), .Q(d_ff_12_q));  // open: Qn, preset, reset
  Pull_Resistor pull_resistor_23 (.node(controlled_buffer_23_out));
  D_Flip_Flop d_ff_13 (
    .D(pull_resistor_17_node), .clk(controlled_buffer_24_out), .Q(d_ff_13_q));  // open: Qn, preset, reset
  assign controlled_buffer_24_out = pull_resistor_4_node ? and_1_out : 1'bz;  // Controlled_Buffer controlled_buffer_24
  D_Flip_Flop d_ff_14 (
    .D(pull_resistor_18_node), .clk(controlled_buffer_24_out), .Q(d_ff_14_q));  // open: Qn, preset, reset
  D_Flip_Flop d_ff_15 (
    .D(pull_resistor_19_node), .clk(controlled_buffer_24_out), .Q(d_ff_15_q));  // open: Qn, preset, reset
  D_Flip_Flop d_ff_16 (
    .D(pull_resistor_20_node), .clk(controlled_buffer_24_out), .Q(d_ff_16_q));  // open: Qn, preset, reset
  Pull_Resistor pull_resistor_24 (.node(controlled_buffer_24_out));
  assign controlled_buffer_25_out = pull_resistor_33_node ? d_ff_1_q : 1'bz;  // Controlled_Buffer controlled_buffer_25
  assign controlled_buffer_26_out = pull_resistor_38_node ? d_ff_1_q : 1'bz;  // Controlled_Buffer controlled_buffer_26
  assign controlled_buffer_27_out = pull_resistor_33_node ? d_ff_2_q : 1'bz;  // Controlled_Buffer controlled_buffer_27
  assign controlled_buffer_28_out = pull_resistor_38_node ? d_ff_2_q : 1'bz;  // Controlled_Buffer controlled_buffer_28
  assign controlled_buffer_29_out = pull_resistor_33_node ? d_ff_3_q : 1'bz;  // Controlled_Buffer controlled_buffer_29
  assign controlled_buffer_30_out = pull_resistor_38_node ? d_ff_3_q : 1'bz;  // Controlled_Buffer controlled_buffer_30
  assign controlled_buffer_31_out = pull_resistor_33_node ? d_ff_4_q : 1'bz;  // Controlled_Buffer controlled_buffer_31
  assign controlled_buffer_32_out = pull_resistor_38_node ? d_ff_4_q : 1'bz;  // Controlled_Buffer controlled_buffer_32
  assign controlled_buffer_25_out = pull_resistor_28_node ? d_ff_5_q : 1'bz;  // Controlled_Buffer controlled_buffer_33
  assign controlled_buffer_26_out = pull_resistor_34_node ? d_ff_5_q : 1'bz;  // Controlled_Buffer controlled_buffer_34
  assign controlled_buffer_27_out = pull_resistor_28_node ? d_ff_6_q : 1'bz;  // Controlled_Buffer controlled_buffer_35
  assign controlled_buffer_28_out = pull_resistor_34_node ? d_ff_6_q : 1'bz;  // Controlled_Buffer controlled_buffer_36
  assign controlled_buffer_29_out = pull_resistor_28_node ? d_ff_7_q : 1'bz;  // Controlled_Buffer controlled_buffer_37
  assign controlled_buffer_30_out = pull_resistor_34_node ? d_ff_7_q : 1'bz;  // Controlled_Buffer controlled_buffer_38
  assign controlled_buffer_31_out = pull_resistor_28_node ? d_ff_8_q : 1'bz;  // Controlled_Buffer controlled_buffer_39
  assign controlled_buffer_32_out = pull_resistor_34_node ? d_ff_8_q : 1'bz;  // Controlled_Buffer controlled_buffer_40
  assign controlled_buffer_25_out = pull_resistor_26_node ? d_ff_9_q : 1'bz;  // Controlled_Buffer controlled_buffer_41
  assign controlled_buffer_26_out = pull_resistor_29_node ? d_ff_9_q : 1'bz;  // Controlled_Buffer controlled_buffer_42
  assign controlled_buffer_27_out = pull_resistor_26_node ? d_ff_10_q : 1'bz;  // Controlled_Buffer controlled_buffer_43
  assign controlled_buffer_28_out = pull_resistor_29_node ? d_ff_10_q : 1'bz;  // Controlled_Buffer controlled_buffer_44
  assign controlled_buffer_29_out = pull_resistor_26_node ? d_ff_11_q : 1'bz;  // Controlled_Buffer controlled_buffer_45
  assign controlled_buffer_30_out = pull_resistor_29_node ? d_ff_11_q : 1'bz;  // Controlled_Buffer controlled_buffer_46
  assign controlled_buffer_31_out = pull_resistor_26_node ? d_ff_12_q : 1'bz;  // Controlled_Buffer controlled_buffer_47
  assign controlled_buffer_32_out = pull_resistor_29_node ? d_ff_12_q : 1'bz;  // Controlled_Buffer controlled_buffer_48
  assign controlled_buffer_25_out = pull_resistor_25_node ? d_ff_13_q : 1'bz;  // Controlled_Buffer controlled_buffer_49
  assign controlled_buffer_26_out = pull_resistor_27_node ? d_ff_13_q : 1'bz;  // Controlled_Buffer controlled_buffer_50
  assign controlled_buffer_27_out = pull_resistor_25_node ? d_ff_14_q : 1'bz;  // Controlled_Buffer controlled_buffer_51
  assign controlled_buffer_28_out = pull_resistor_27_node ? d_ff_14_q : 1'bz;  // Controlled_Buffer controlled_buffer_52
  assign controlled_buffer_29_out = pull_resistor_25_node ? d_ff_15_q : 1'bz;  // Controlled_Buffer controlled_buffer_53
  assign controlled_buffer_30_out = pull_resistor_27_node ? d_ff_15_q : 1'bz;  // Controlled_Buffer controlled_buffer_54
  assign controlled_buffer_31_out = pull_resistor_25_node ? d_ff_16_q : 1'bz;  // Controlled_Buffer controlled_buffer_55
  assign controlled_buffer_32_out = pull_resistor_27_node ? d_ff_16_q : 1'bz;  // Controlled_Buffer controlled_buffer_56
  Decoder #(.select(2)) decoder_2 (
    .out0(decoder_2_out0), .out1(decoder_2_out1), .out2(decoder_2_out2), .out3(decoder_2_out3),
    .sel(pull_resistor_30_node));  // open: en
  Decoder #(.select(2)) decoder_3 (
    .out0(decoder_3_out0), .out1(decoder_3_out1), .out2(decoder_3_out2), .out3(decoder_3_out3),
    .sel(pull_resistor_32_node));  // open: en
  Pull_Resistor pull_resistor_25 (.node(pull_resistor_25_node));
  Pull_Resistor pull_resistor_26 (.node(pull_resistor_26_node));
  assign pull_resistor_25_node = or_1_out ? decoder_2_out3 : 1'bz;  // Controlled_Buffer controlled_buffer_57
  assign pull_resistor_26_node = or_1_out ? decoder_2_out2 : 1'bz;  // Controlled_Buffer controlled_buffer_58
  Pull_Resistor pull_resistor_27 (.node(pull_resistor_27_node));
  assign pull_resistor_27_node = or_2_out ? decoder_3_out3 : 1'bz;  // Controlled_Buffer controlled_buffer_59
  Pull_Resistor pull_resistor_28 (.node(pull_resistor_28_node));
  assign pull_resistor_28_node = or_1_out ? decoder_2_out1 : 1'bz;  // Controlled_Buffer controlled_buffer_60
  Pull_Resistor pull_resistor_29 (.node(pull_resistor_29_node));
  assign pull_resistor_29_node = or_2_out ? decoder_3_out2 : 1'bz;  // Controlled_Buffer controlled_buffer_61
  Pull_Resistor pull_resistor_30 (.node(pull_resistor_30_node[0]));
  Pull_Resistor pull_resistor_31 (.node(pull_resistor_31_node[0]));
  Pull_Resistor pull_resistor_32 (.node(pull_resistor_32_node[0]));
  Pull_Resistor pull_resistor_33 (.node(pull_resistor_33_node));
  assign pull_resistor_33_node = or_1_out ? decoder_2_out0 : 1'bz;  // Controlled_Buffer controlled_buffer_62
  Pull_Resistor pull_resistor_34 (.node(pull_resistor_34_node));
  assign pull_resistor_34_node = or_2_out ? decoder_3_out1 : 1'bz;  // Controlled_Buffer controlled_buffer_63
  Pull_Resistor pull_resistor_35 (.node(pull_resistor_30_node[1]));
  Pull_Resistor pull_resistor_36 (.node(pull_resistor_31_node[1]));
  Pull_Resistor pull_resistor_37 (.node(pull_resistor_32_node[1]));
  Pull_Resistor pull_resistor_38 (.node(pull_resistor_38_node));
  assign pull_resistor_38_node = or_2_out ? decoder_3_out0 : 1'bz;  // Controlled_Buffer controlled_buffer_64
  Pull_Resistor pull_resistor_39 (.node(controlled_buffer_25_out));
  Pull_Resistor pull_resistor_40 (.node(controlled_buffer_27_out));
  Pull_Resistor pull_resistor_41 (.node(controlled_buffer_29_out));
  Pull_Resistor pull_resistor_42 (.node(controlled_buffer_31_out));
  Pull_Resistor pull_resistor_43 (.node(controlled_buffer_26_out));
  Pull_Resistor pull_resistor_44 (.node(controlled_buffer_28_out));
  Pull_Resistor pull_resistor_45 (.node(controlled_buffer_30_out));
  Pull_Resistor pull_resistor_46 (.node(controlled_buffer_32_out));
  Pull_Resistor pull_resistor_47 (.node(pull_resistor_47_node[0]));
  Decoder #(.select(2)) decoder_4 (
    .out0(decoder_4_out0), .out1(decoder_4_out1), .out2(decoder_4_out2), .out3(decoder_4_out3),
    .sel(pull_resistor_47_node));  // open: en
  RAM ram_1 ();  // open: addr, we, oe, clk, din, dout
  nor nor_1 (nor_1_out, d_ff_1_q, d_ff_2_q, d_ff_3_q, d_ff_4_q);
  assign controlled_buffer_65_out = pull_resistor_49_node ? nor_1_out : 1'bz;  // Controlled_Buffer controlled_buffer_65
  nor nor_2 (nor_2_out, d_ff_5_q, d_ff_6_q, d_ff_7_q, d_ff_8_q);
  nor nor_3 (nor_3_out, d_ff_9_q, d_ff_10_q, d_ff_11_q, d_ff_12_q);
  nor nor_4 (nor_4_out, d_ff_13_q, d_ff_14_q, d_ff_15_q, d_ff_16_q);
  Pull_Resistor pull_resistor_48 (.node(pull_resistor_48_node));
  Pull_Resistor pull_resistor_49 (.node(pull_resistor_49_node));
  assign pull_resistor_48_node = decoder_6_out14 ? decoder_4_out1 : 1'bz;  // Controlled_Buffer controlled_buffer_66
  assign pull_resistor_49_node = decoder_6_out14 ? decoder_4_out0 : 1'bz;  // Controlled_Buffer controlled_buffer_67
  Pull_Resistor pull_resistor_50 (.node(pull_resistor_47_node[1]));
  assign pull_resistor_47_node[1] = decoder_6_out14 ? d_ff_29_q : 1'bz;  // Controlled_Buffer controlled_buffer_68
  assign pull_resistor_47_node[0] = decoder_6_out14 ? d_ff_28_q : 1'bz;  // Controlled_Buffer controlled_buffer_69
  assign pull_resistor_30_node[1] = or_1_out ? d_ff_29_q : 1'bz;  // Controlled_Buffer controlled_buffer_70
  assign pull_resistor_30_node[0] = or_1_out ? d_ff_28_q : 1'bz;  // Controlled_Buffer controlled_buffer_71
  assign pull_resistor_31_node[1] = or_1_out ? d_ff_29_q : 1'bz;  // Controlled_Buffer controlled_buffer_72
  assign pull_resistor_31_node[0] = or_1_out ? d_ff_28_q : 1'bz;  // Controlled_Buffer controlled_buffer_73
  assign pull_resistor_32_node[1] = or_2_out ? d_ff_27_q : 1'bz;  // Controlled_Buffer controlled_buffer_74
  assign pull_resistor_32_node[0] = or_2_out ? d_ff_26_q : 1'bz;  // Controlled_Buffer controlled_buffer_75
  assign controlled_buffer_65_out = pull_resistor_48_node ? nor_2_out : 1'bz;  // Controlled_Buffer controlled_buffer_76
  assign controlled_buffer_65_out = pull_resistor_52_node ? nor_3_out : 1'bz;  // Controlled_Buffer controlled_buffer_77
  assign controlled_buffer_65_out = pull_resistor_51_node ? nor_4_out : 1'bz;  // Controlled_Buffer controlled_buffer_78
  Pull_Resistor pull_resistor_51 (.node(pull_resistor_51_node));
  Pull_Resistor pull_resistor_52 (.node(pull_resistor_52_node));
  assign pull_resistor_51_node = decoder_6_out14 ? decoder_4_out3 : 1'bz;  // Controlled_Buffer controlled_buffer_79
  assign pull_resistor_52_node = decoder_6_out14 ? decoder_4_out2 : 1'bz;  // Controlled_Buffer controlled_buffer_80
  LED led_1 (.in(controlled_buffer_65_out));
  Pull_Resistor pull_resistor_53 (.node(controlled_buffer_65_out));
  or or_1 (or_1_out, decoder_6_out1, decoder_6_out2, decoder_6_out3, decoder_6_out4, decoder_6_out5, decoder_6_out6, decoder_6_out7, decoder_6_out8, decoder_6_out9, decoder_6_out10, decoder_6_out11, decoder_6_out12);
  or or_2 (or_2_out, decoder_6_out3, decoder_6_out4, decoder_6_out5, decoder_6_out12, decoder_6_out6, decoder_6_out7, decoder_6_out8);
  D_Flip_Flop #(.trigger("falling")) d_ff_17 (
    .D(or_3_out), .clk(clock_1_out), .Q(d_ff_17_q));  // open: Qn, preset, reset
  and and_2 (and_2_out, or_3_out, not_1_out);
  not not_1 (not_1_out, d_ff_17_q);
  D_Flip_Flop #(.trigger("falling")) d_ff_18 (
    .D(and_2_out), .clk(clock_1_out), .Q(d_ff_18_q));  // open: Qn, preset, reset
  not not_2 (not_2_out, d_ff_44_q);
  and and_3 (and_3_out, decoder_6_out15, not_2_out);
  POR #(.porsize(1)) por_1 (.out(por_1_out));
  not not_3 (not_3_out, controlled_buffer_65_out);
  and and_4 (and_4_out, decoder_6_out14, not_3_out);
  or or_3 (or_3_out, and_3_out, and_4_out);
  and and_5 (and_5_out, d_ff_21_q, decoder_5_out0);
  Clock clock_1 (.out(clock_1_out));
  assign controlled_buffer_81_out = decoder_6_out15 ? controlled_buffer_65_out : 1'bz;  // Controlled_Buffer controlled_buffer_81
  Pull_Resistor pull_resistor_54 (.node(controlled_buffer_81_out));
  assign controlled_buffer_82_out = decoder_6_out14 ? d_ff_44_q : 1'bz;  // Controlled_Buffer controlled_buffer_82
  Pull_Resistor pull_resistor_55 (.node(controlled_buffer_82_out));
  or or_4 (or_4_out, controlled_buffer_82_out, controlled_buffer_81_out, decoder_6_out13);
  D_Flip_Flop #(.trigger("falling")) d_ff_19 (.D(or_4_out), .clk(and_5_out), .Q(d_ff_19_q));  // open: Qn, preset, reset
  D_Flip_Flop #(.trigger("falling")) d_ff_20 (
    .D(d_ff_20_qn), .clk(pull_resistor_56_node), .Q(d_ff_20_q), .Qn(d_ff_20_qn), .reset(and_6_out));  // open: preset
  Pull_Resistor pull_resistor_56 (.node(pull_resistor_56_node));
  assign pull_resistor_56_node = d_ff_20_qn ? and_5_out : 1'bz;  // Controlled_Buffer controlled_buffer_83
  D_Flip_Flop #(.trigger("falling")) d_ff_21 (
    .D(d_ff_21_qn), .clk(clock_1_out), .Q(d_ff_21_q), .Qn(d_ff_21_qn));  // open: preset, reset
  assign controlled_buffer_84_out = decoder_6_out12 ? controlled_buffer_32_out : 1'bz;  // Controlled_Buffer controlled_buffer_84
  and and_6 (and_6_out, or_4_out, not_4_out);
  not not_4 (not_4_out, d_ff_19_q);
  or or_5 (or_5_out, por_1_out, d_ff_20_q);
  Pull_Resistor pull_resistor_57 (.node(pull_resistor_57_node));
  assign pull_resistor_57_node = d_ff_24_qn ? decoder_5_out0 : 1'bz;  // Controlled_Buffer controlled_buffer_85
  D_Flip_Flop #(.trigger("falling")) d_ff_22 (
    .D(d_ff_22_qn), .clk(d_ff_21_q), .Q(d_ff_22_q[0]), .Qn(d_ff_22_qn));  // open: preset, reset
  assign controlled_buffer_86_out = decoder_6_out12 ? controlled_buffer_30_out : 1'bz;  // Controlled_Buffer controlled_buffer_86
  assign controlled_buffer_87_out = decoder_6_out12 ? controlled_buffer_28_out : 1'bz;  // Controlled_Buffer controlled_buffer_87
  nor nor_5 (nor_5_out, and_6_out, nor_6_out);
  nor nor_6 (nor_6_out, nor_5_out, or_5_out);
  D_Flip_Flop d_ff_23 (.D(nor_6_out), .clk(decoder_5_out1), .Q(d_ff_23_q), .reset(not_5_out));  // open: Qn, preset
  not not_5 (not_5_out, nor_6_out);
  D_Flip_Flop #(.trigger("falling")) d_ff_24 (
    .D(d_ff_24_qn), .clk(pull_resistor_57_node), .Q(d_ff_24_q), .Qn(d_ff_24_qn), .reset(d_ff_23_q));  // open: preset
  D_Flip_Flop #(.trigger("falling")) d_ff_25 (
    .D(d_ff_25_qn), .clk(d_ff_22_q[0]), .Q(d_ff_22_q[1]), .Qn(d_ff_25_qn));  // open: preset, reset
  assign controlled_buffer_88_out = decoder_6_out12 ? controlled_buffer_26_out : 1'bz;  // Controlled_Buffer controlled_buffer_88
  Pull_Resistor pull_resistor_58 (.node(pull_resistor_58_node));
  assign pull_resistor_58_node = d_ff_24_q ? decoder_5_out0 : 1'bz;  // Controlled_Buffer controlled_buffer_89
  Decoder #(.select(2)) decoder_5 (
    .out0(decoder_5_out0), .out1(decoder_5_out1), .out2(decoder_5_out2), .out3(decoder_5_out3),
    .sel(d_ff_22_q));  // open: en
  not not_6 (not_6_out, d_ff_23_q);
  Pull_Resistor pull_resistor_59 (.node(pull_resistor_59_node));
  assign pull_resistor_59_node = not_6_out ? rom_1_data[0] : 1'bz;  // Controlled_Buffer controlled_buffer_90
  and and_7 (and_7_out, d_ff_21_q, decoder_5_out1);
  and and_8 (and_8_out, pull_resistor_58_node, d_ff_21_q);
  not not_7 (not_7_out, clock_1_out);
  D_Flip_Flop d_ff_26 (.D(pull_resistor_59_node), .clk(and_7_out), .Q(d_ff_26_q));  // open: Qn, preset, reset
  Pull_Resistor pull_resistor_60 (.node(d_ff_23_q));
  and and_9 (and_9_out, d_ff_18_q, not_7_out);
  D_Flip_Flop d_ff_27 (.D(pull_resistor_61_node), .clk(and_7_out), .Q(d_ff_27_q));  // open: Qn, preset, reset
  Pull_Resistor pull_resistor_61 (.node(pull_resistor_61_node));
  assign pull_resistor_61_node = not_6_out ? rom_1_data[1] : 1'bz;  // Controlled_Buffer controlled_buffer_91
  or or_6 (or_6_out, and_8_out, and_9_out);
  Pull_Resistor pull_resistor_62 (.node(pull_resistor_62_node));
  assign pull_resistor_62_node = not_6_out ? rom_1_data[2] : 1'bz;  // Controlled_Buffer controlled_buffer_92
  ROM rom_1 (.addr(d_ff_30_q), .data(rom_1_data));
  Decoder #(.select(4)) decoder_6 (
    .out1(decoder_6_out1), .out2(decoder_6_out2), .out3(decoder_6_out3), .out4(decoder_6_out4),
    .out5(decoder_6_out5), .out6(decoder_6_out6), .out7(decoder_6_out7), .out8(decoder_6_out8),
    .out9(decoder_6_out9), .out10(decoder_6_out10), .out11(decoder_6_out11), .out12(decoder_6_out12),
    .out13(decoder_6_out13), .out14(decoder_6_out14), .out15(decoder_6_out15), .sel(d_ff_31_q));  // open: out0, en
  D_Flip_Flop d_ff_28 (.D(pull_resistor_62_node), .clk(and_7_out), .Q(d_ff_28_q));  // open: Qn, preset, reset
  assign controlled_buffer_93_out = not_6_out ? d_ff_30_qn : 1'bz;  // Controlled_Buffer controlled_buffer_93
  D_Flip_Flop d_ff_29 (.D(pull_resistor_63_node), .clk(and_7_out), .Q(d_ff_29_q));  // open: Qn, preset, reset
  Pull_Resistor pull_resistor_63 (.node(pull_resistor_63_node));
  assign pull_resistor_63_node = not_6_out ? rom_1_data[3] : 1'bz;  // Controlled_Buffer controlled_buffer_94
  assign controlled_buffer_93_out = d_ff_23_q ? rom_1_data[0] : 1'bz;  // Controlled_Buffer controlled_buffer_95
  D_Flip_Flop #(.trigger("falling")) d_ff_30 (
    .D(controlled_buffer_93_out), .clk(controlled_buffer_96_out), .Q(d_ff_30_q[0]), .Qn(d_ff_30_qn));  // open: preset, reset
  assign controlled_buffer_96_out = not_6_out ? or_6_out : 1'bz;  // Controlled_Buffer controlled_buffer_96
  assign controlled_buffer_96_out = d_ff_23_q ? decoder_5_out1 : 1'bz;  // Controlled_Buffer controlled_buffer_97
  D_Flip_Flop d_ff_31 (.D(pull_resistor_64_node), .clk(and_7_out), .Q(d_ff_31_q[0]));  // open: Qn, preset, reset
  Pull_Resistor pull_resistor_64 (.node(pull_resistor_64_node));
  assign pull_resistor_64_node = not_6_out ? rom_1_data[4] : 1'bz;  // Controlled_Buffer controlled_buffer_98
  Pull_Resistor pull_resistor_65 (.node(pull_resistor_65_node));
  assign pull_resistor_65_node = not_6_out ? rom_1_data[5] : 1'bz;  // Controlled_Buffer controlled_buffer_99
  assign controlled_buffer_100_out = d_ff_23_q ? rom_1_data[1] : 1'bz;  // Controlled_Buffer controlled_buffer_100
  assign controlled_buffer_100_out = not_6_out ? d_ff_33_qn : 1'bz;  // Controlled_Buffer controlled_buffer_101
  assign controlled_buffer_102_out = not_6_out ? d_ff_30_q[0] : 1'bz;  // Controlled_Buffer controlled_buffer_102
  assign controlled_buffer_102_out = d_ff_23_q ? controlled_buffer_96_out : 1'bz;  // Controlled_Buffer controlled_buffer_103
  D_Flip_Flop d_ff_32 (.D(pull_resistor_65_node), .clk(and_7_out), .Q(d_ff_31_q[1]));  // open: Qn, preset, reset
  D_Flip_Flop #(.trigger("falling")) d_ff_33 (
    .D(controlled_buffer_100_out), .clk(controlled_buffer_102_out), .Q(d_ff_30_q[1]), .Qn(d_ff_33_qn));  // open: preset, reset
  D_Flip_Flop d_ff_34 (.D(pull_resistor_66_node), .clk(and_7_out), .Q(d_ff_31_q[2]));  // open: Qn, preset, reset
  Pull_Resistor pull_resistor_66 (.node(pull_resistor_66_node));
  assign pull_resistor_66_node = not_6_out ? rom_1_data[6] : 1'bz;  // Controlled_Buffer controlled_buffer_104
  assign controlled_buffer_105_out = d_ff_23_q ? rom_1_data[2] : 1'bz;  // Controlled_Buffer controlled_buffer_105
  assign controlled_buffer_105_out = not_6_out ? d_ff_35_qn : 1'bz;  // Controlled_Buffer controlled_buffer_106
  assign controlled_buffer_107_out = not_6_out ? d_ff_30_q[1] : 1'bz;  // Controlled_Buffer controlled_buffer_107
  assign controlled_buffer_107_out = d_ff_23_q ? controlled_buffer_102_out : 1'bz;  // Controlled_Buffer controlled_buffer_108
  Pull_Resistor pull_resistor_67 (.node(pull_resistor_67_node));
  assign pull_resistor_67_node = not_6_out ? rom_1_data[7] : 1'bz;  // Controlled_Buffer controlled_buffer_109
  D_Flip_Flop #(.trigger("falling")) d_ff_35 (
    .D(controlled_buffer_105_out), .clk(controlled_buffer_107_out), .Q(d_ff_30_q[2]), .Qn(d_ff_35_qn));  // open: preset, reset
  D_Flip_Flop d_ff_36 (.D(pull_resistor_67_node), .clk(and_7_out), .Q(d_ff_31_q[3]));  // open: Qn, preset, reset
  assign controlled_buffer_110_out = not_6_out ? d_ff_37_qn : 1'bz;  // Controlled_Buffer controlled_buffer_110
  assign controlled_buffer_110_out = d_ff_23_q ? rom_1_data[3] : 1'bz;  // Controlled_Buffer controlled_buffer_111
  D_Flip_Flop #(.trigger("falling")) d_ff_37 (
    .D(controlled_buffer_110_out), .clk(controlled_buffer_112_out), .Q(d_ff_30_q[3]), .Qn(d_ff_37_qn));  // open: preset, reset
  assign controlled_buffer_112_out = not_6_out ? d_ff_30_q[2] : 1'bz;  // Controlled_Buffer controlled_buffer_112
  assign controlled_buffer_112_out = d_ff_23_q ? controlled_buffer_107_out : 1'bz;  // Controlled_Buffer controlled_buffer_113
  assign controlled_buffer_114_out = d_ff_23_q ? rom_1_data[4] : 1'bz;  // Controlled_Buffer controlled_buffer_114
  assign controlled_buffer_114_out = not_6_out ? d_ff_38_qn : 1'bz;  // Controlled_Buffer controlled_buffer_115
  assign controlled_buffer_116_out = not_6_out ? d_ff_30_q[3] : 1'bz;  // Controlled_Buffer controlled_buffer_116
  assign controlled_buffer_116_out = d_ff_23_q ? controlled_buffer_112_out : 1'bz;  // Controlled_Buffer controlled_buffer_117
  D_Flip_Flop #(.trigger("falling")) d_ff_38 (
    .D(controlled_buffer_114_out), .clk(controlled_buffer_116_out), .Q(d_ff_30_q[4]), .Qn(d_ff_38_qn));  // open: preset, reset
  assign controlled_buffer_118_out = not_6_out ? d_ff_39_qn : 1'bz;  // Controlled_Buffer controlled_buffer_118
  assign controlled_buffer_119_out = not_6_out ? d_ff_30_q[4] : 1'bz;  // Controlled_Buffer controlled_buffer_119
  assign controlled_buffer_119_out = d_ff_23_q ? controlled_buffer_116_out : 1'bz;  // Controlled_Buffer controlled_buffer_120
  assign controlled_buffer_118_out = d_ff_23_q ? rom_1_data[5] : 1'bz;  // Controlled_Buffer controlled_buffer_121
  D_Flip_Flop #(.trigger("falling")) d_ff_39 (
    .D(controlled_buffer_118_out), .clk(controlled_buffer_119_out), .Q(d_ff_30_q[5]), .Qn(d_ff_39_qn));  // open: preset, reset
  assign controlled_buffer_122_out = not_6_out ? d_ff_40_qn : 1'bz;  // Controlled_Buffer controlled_buffer_122
  assign controlled_buffer_122_out = d_ff_23_q ? rom_1_data[6] : 1'bz;  // Controlled_Buffer controlled_buffer_123
  D_Flip_Flop #(.trigger("falling")) d_ff_40 (
    .D(controlled_buffer_122_out), .clk(controlled_buffer_124_out), .Q(d_ff_30_q[6]), .Qn(d_ff_40_qn));  // open: preset, reset
  assign controlled_buffer_124_out = not_6_out ? d_ff_30_q[5] : 1'bz;  // Controlled_Buffer controlled_buffer_124
  assign controlled_buffer_124_out = d_ff_23_q ? controlled_buffer_119_out : 1'bz;  // Controlled_Buffer controlled_buffer_125
  assign controlled_buffer_126_out = d_ff_23_q ? rom_1_data[7] : 1'bz;  // Controlled_Buffer controlled_buffer_126
  assign controlled_buffer_126_out = not_6_out ? d_ff_41_qn : 1'bz;  // Controlled_Buffer controlled_buffer_127
  assign controlled_buffer_128_out = not_6_out ? d_ff_30_q[6] : 1'bz;  // Controlled_Buffer controlled_buffer_128
  assign controlled_buffer_128_out = d_ff_23_q ? controlled_buffer_124_out : 1'bz;  // Controlled_Buffer controlled_buffer_129
  D_Flip_Flop #(.trigger("falling")) d_ff_41 (
    .D(controlled_buffer_126_out), .clk(controlled_buffer_128_out), .Q(d_ff_30_q[7]), .Qn(d_ff_41_qn));  // open: preset, reset
  and and_10 (and_10_out, decoder_6_out10, decoder_6_out9);
  assign controlled_buffer_130_out = and_10_out ? d_ff_26_q : 1'bz;  // Controlled_Buffer controlled_buffer_130
  or or_7 (or_7_out, decoder_6_out3, decoder_6_out4, decoder_6_out5);
  Pull_Resistor pull_resistor_68 (.node(controlled_buffer_130_out));
  or or_8 (or_8_out, decoder_6_out3, decoder_6_out4);
  not not_8 (not_8_out, clock_1_out);
  and and_11 (and_11_out, not_8_out, decoder_5_out2);
  assign controlled_buffer_131_out = decoder_6_out9 ? decoder_5_out2 : 1'bz;  // Controlled_Buffer controlled_buffer_131
  assign controlled_buffer_132_out = decoder_6_out5 ? controlled_buffer_31_out : 1'bz;  // Controlled_Buffer controlled_buffer_132
  assign controlled_buffer_132_out = or_8_out ? controlled_buffer_31_out : 1'bz;  // Controlled_Buffer controlled_buffer_133
  assign controlled_buffer_134_out = decoder_6_out5 ? controlled_buffer_29_out : 1'bz;  // Controlled_Buffer controlled_buffer_134
  assign controlled_buffer_134_out = or_8_out ? controlled_buffer_29_out : 1'bz;  // Controlled_Buffer controlled_buffer_135
  assign controlled_buffer_136_out = decoder_6_out5 ? controlled_buffer_27_out : 1'bz;  // Controlled_Buffer controlled_buffer_136
  assign controlled_buffer_136_out = or_8_out ? controlled_buffer_27_out : 1'bz;  // Controlled_Buffer controlled_buffer_137
  assign controlled_buffer_138_out = decoder_6_out5 ? controlled_buffer_25_out : 1'bz;  // Controlled_Buffer controlled_buffer_138
  assign controlled_buffer_138_out = or_8_out ? controlled_buffer_25_out : 1'bz;  // Controlled_Buffer controlled_buffer_139
  D_Flip_Flop #(.trigger("falling")) d_ff_42 (
    .D(decoder_6_out9), .clk(and_11_out), .Q(d_ff_42_q));  // open: Qn, preset, reset
  assign controlled_buffer_140_out = decoder_6_out9 ? controlled_buffer_130_out : 1'bz;  // Controlled_Buffer controlled_buffer_140
  Pull_Resistor pull_resistor_69 (.node(controlled_buffer_131_out));
  not not_9 (not_9_out, clock_1_out);
  D_Flip_Flop #(.trigger("falling")) d_ff_43 (
    .D(decoder_6_out10), .clk(and_12_out), .Q(d_ff_43_q));  // open: Qn, preset, reset
  not not_10 (not_10_out, clock_1_out);
  and and_12 (and_12_out, not_10_out, decoder_5_out2);
  not not_11 (not_11_out, clock_1_out);
  Pull_Resistor pull_resistor_70 (.node(controlled_buffer_132_out));
  assign controlled_buffer_141_out = or_8_out ? controlled_buffer_32_out : 1'bz;  // Controlled_Buffer controlled_buffer_141
  Pull_Resistor pull_resistor_71 (.node(controlled_buffer_141_out));
  not not_12 (not_12_out, controlled_buffer_32_out);
  assign controlled_buffer_141_out = decoder_6_out5 ? not_12_out : 1'bz;  // Controlled_Buffer controlled_buffer_142
  Pull_Resistor pull_resistor_72 (.node(pull_resistor_72_node));
  assign pull_resistor_72_node = decoder_6_out5 ? 1'b1 : 1'bz;  // Controlled_Buffer controlled_buffer_143
  Pull_Resistor pull_resistor_73 (.node(controlled_buffer_134_out));
  assign controlled_buffer_144_out = or_8_out ? controlled_buffer_30_out : 1'bz;  // Controlled_Buffer controlled_buffer_144
  Pull_Resistor pull_resistor_74 (.node(controlled_buffer_144_out));
  not not_13 (not_13_out, controlled_buffer_30_out);
  assign controlled_buffer_144_out = decoder_6_out5 ? not_13_out : 1'bz;  // Controlled_Buffer controlled_buffer_145
  Pull_Resistor pull_resistor_75 (.node(controlled_buffer_136_out));
  assign controlled_buffer_146_out = or_8_out ? controlled_buffer_28_out : 1'bz;  // Controlled_Buffer controlled_buffer_146
  Pull_Resistor pull_resistor_76 (.node(controlled_buffer_146_out));
  not not_14 (not_14_out, controlled_buffer_28_out);
  assign controlled_buffer_146_out = decoder_6_out5 ? not_14_out : 1'bz;  // Controlled_Buffer controlled_buffer_147
  Pull_Resistor pull_resistor_77 (.node(controlled_buffer_138_out));
  assign controlled_buffer_148_out = or_8_out ? controlled_buffer_26_out : 1'bz;  // Controlled_Buffer controlled_buffer_148
  Pull_Resistor pull_resistor_78 (.node(controlled_buffer_148_out));
  not not_15 (not_15_out, controlled_buffer_26_out);
  assign controlled_buffer_148_out = decoder_6_out5 ? not_15_out : 1'bz;  // Controlled_Buffer controlled_buffer_149
  and and_13 (and_13_out, decoder_6_out9, not_16_out);
  not not_16 (not_16_out, d_ff_42_q);
  not not_17 (not_17_out, controlled_buffer_140_out);
  Pull_Resistor pull_resistor_79 (.node(controlled_buffer_140_out));
  and and_14 (and_14_out, d_ff_21_q, controlled_buffer_131_out);
  and and_15 (and_15_out, not_9_out, decoder_6_out9, decoder_5_out2);
  and and_16 (and_16_out, decoder_6_out9, decoder_5_out3);
  not not_18 (not_18_out, d_ff_43_q);
  and and_17 (and_17_out, d_ff_21_q, decoder_5_out2);
  and and_18 (and_18_out, not_11_out, decoder_6_out10, decoder_5_out2);
  xor xor_1 (xor_1_out, controlled_buffer_132_out, controlled_buffer_141_out);
  xor xor_2 (xor_2_out, controlled_buffer_134_out, controlled_buffer_144_out);
  xor xor_3 (xor_3_out, controlled_buffer_136_out, controlled_buffer_146_out);
  xor xor_4 (xor_4_out, controlled_buffer_138_out, controlled_buffer_148_out);
  not not_19 (not_19_out, and_14_out);
  assign controlled_buffer_150_out = controlled_buffer_140_out ? not_19_out : 1'bz;  // Controlled_Buffer controlled_buffer_150
  and and_19 (and_19_out, decoder_6_out10, not_18_out);
  not not_20 (not_20_out, and_19_out);
  assign controlled_buffer_151_out = and_19_out ? and_18_out : 1'bz;  // Controlled_Buffer controlled_buffer_151
  xor xor_5 (xor_5_out, xor_1_out, pull_resistor_72_node);
  and and_20 (and_20_out, pull_resistor_72_node, xor_1_out);
  and and_21 (and_21_out, controlled_buffer_141_out, controlled_buffer_132_out);
  xor xor_6 (xor_6_out, xor_2_out, or_9_out);
  and and_22 (and_22_out, or_9_out, xor_2_out);
  and and_23 (and_23_out, controlled_buffer_144_out, controlled_buffer_134_out);
  xor xor_7 (xor_7_out, xor_3_out, or_10_out);
  and and_24 (and_24_out, or_10_out, xor_3_out);
  and and_25 (and_25_out, controlled_buffer_146_out, controlled_buffer_136_out);
  xor xor_8 (xor_8_out, xor_4_out, or_11_out);
  and and_26 (and_26_out, or_11_out, xor_4_out);
  and and_27 (and_27_out, controlled_buffer_148_out, controlled_buffer_138_out);
  Pull_Resistor pull_resistor_80 (.node(pull_resistor_80_node));
  assign pull_resistor_80_node = decoder_6_out6 ? controlled_buffer_25_out : 1'bz;  // Controlled_Buffer controlled_buffer_152
  assign controlled_buffer_153_out = decoder_6_out6 ? controlled_buffer_26_out : 1'bz;  // Controlled_Buffer controlled_buffer_153
  Pull_Resistor pull_resistor_81 (.node(pull_resistor_81_node));
  assign pull_resistor_81_node = decoder_6_out6 ? controlled_buffer_27_out : 1'bz;  // Controlled_Buffer controlled_buffer_154
  assign controlled_buffer_155_out = decoder_6_out6 ? controlled_buffer_28_out : 1'bz;  // Controlled_Buffer controlled_buffer_155
  Pull_Resistor pull_resistor_82 (.node(pull_resistor_82_node));
  assign pull_resistor_82_node = decoder_6_out6 ? controlled_buffer_29_out : 1'bz;  // Controlled_Buffer controlled_buffer_156
  assign controlled_buffer_157_out = decoder_6_out6 ? controlled_buffer_30_out : 1'bz;  // Controlled_Buffer controlled_buffer_157
  Pull_Resistor pull_resistor_83 (.node(pull_resistor_83_node));
  assign pull_resistor_83_node = decoder_6_out6 ? controlled_buffer_31_out : 1'bz;  // Controlled_Buffer controlled_buffer_158
  assign controlled_buffer_159_out = decoder_6_out6 ? controlled_buffer_32_out : 1'bz;  // Controlled_Buffer controlled_buffer_159
  Pull_Resistor pull_resistor_84 (.node(pull_resistor_84_node));
  assign pull_resistor_84_node = decoder_6_out7 ? controlled_buffer_25_out : 1'bz;  // Controlled_Buffer controlled_buffer_160
  assign controlled_buffer_161_out = decoder_6_out7 ? controlled_buffer_26_out : 1'bz;  // Controlled_Buffer controlled_buffer_161
  Pull_Resistor pull_resistor_85 (.node(pull_resistor_85_node));
  assign pull_resistor_85_node = decoder_6_out7 ? controlled_buffer_27_out : 1'bz;  // Controlled_Buffer controlled_buffer_162
  assign controlled_buffer_163_out = decoder_6_out7 ? controlled_buffer_28_out : 1'bz;  // Controlled_Buffer controlled_buffer_163
  Pull_Resistor pull_resistor_86 (.node(pull_resistor_86_node));
  assign pull_resistor_86_node = decoder_6_out7 ? controlled_buffer_29_out : 1'bz;  // Controlled_Buffer controlled_buffer_164
  assign controlled_buffer_165_out = decoder_6_out7 ? controlled_buffer_30_out : 1'bz;  // Controlled_Buffer controlled_buffer_165
  Pull_Resistor pull_resistor_87 (.node(pull_resistor_87_node));
  assign pull_resistor_87_node = decoder_6_out7 ? controlled_buffer_31_out : 1'bz;  // Controlled_Buffer controlled_buffer_166
  assign controlled_buffer_167_out = decoder_6_out7 ? controlled_buffer_32_out : 1'bz;  // Controlled_Buffer controlled_buffer_167
  Pull_Resistor pull_resistor_88 (.node(pull_resistor_88_node));
  assign pull_resistor_88_node = decoder_6_out8 ? controlled_buffer_25_out : 1'bz;  // Controlled_Buffer controlled_buffer_168
  assign controlled_buffer_169_out = decoder_6_out8 ? controlled_buffer_26_out : 1'bz;  // Controlled_Buffer controlled_buffer_169
  Pull_Resistor pull_resistor_89 (.node(pull_resistor_89_node));
  assign pull_resistor_89_node = decoder_6_out8 ? controlled_buffer_27_out : 1'bz;  // Controlled_Buffer controlled_buffer_170
  assign controlled_buffer_171_out = decoder_6_out8 ? controlled_buffer_28_out : 1'bz;  // Controlled_Buffer controlled_buffer_171
  Pull_Resistor pull_resistor_90 (.node(pull_resistor_90_node));
  assign pull_resistor_90_node = decoder_6_out8 ? controlled_buffer_29_out : 1'bz;  // Controlled_Buffer controlled_buffer_172
  assign controlled_buffer_173_out = decoder_6_out8 ? controlled_buffer_30_out : 1'bz;  // Controlled_Buffer controlled_buffer_173
  Pull_Resistor pull_resistor_91 (.node(pull_resistor_91_node));
  assign pull_resistor_91_node = decoder_6_out8 ? controlled_buffer_31_out : 1'bz;  // Controlled_Buffer controlled_buffer_174
  assign controlled_buffer_175_out = decoder_6_out8 ? controlled_buffer_32_out : 1'bz;  // Controlled_Buffer controlled_buffer_175
  not not_21 (not_21_out, and_13_out);
  assign controlled_buffer_176_out = and_13_out ? controlled_buffer_31_out : 1'bz;  // Controlled_Buffer controlled_buffer_176
  Pull_Resistor pull_resistor_92 (.node(controlled_buffer_176_out));
  assign controlled_buffer_176_out = not_21_out ? d_ff_45_qn : 1'bz;  // Controlled_Buffer controlled_buffer_177
  assign controlled_buffer_150_out = not_17_out ? and_14_out : 1'bz;  // Controlled_Buffer controlled_buffer_178
  Pull_Resistor pull_resistor_93 (.node(controlled_buffer_150_out));
  assign controlled_buffer_179_out = not_22_out ? controlled_buffer_150_out : 1'bz;  // Controlled_Buffer controlled_buffer_179
  not not_22 (not_22_out, and_13_out);
  assign controlled_buffer_151_out = not_20_out ? and_17_out : 1'bz;  // Controlled_Buffer controlled_buffer_180
  and and_28 (and_28_out, decoder_6_out10, decoder_5_out3);
  or or_9 (or_9_out, and_20_out, and_21_out);
  or or_10 (or_10_out, and_22_out, and_23_out);
  or or_11 (or_11_out, and_24_out, and_25_out);
  D_Flip_Flop d_ff_44 (.D(or_12_out), .clk(pull_resistor_94_node), .Q(d_ff_44_q));  // open: Qn, preset, reset
  or or_12 (or_12_out, and_26_out, and_27_out);
  Pull_Resistor pull_resistor_94 (.node(pull_resistor_94_node));
  assign pull_resistor_94_node = or_8_out ? decoder_5_out2 : 1'bz;  // Controlled_Buffer controlled_buffer_181
  and and_29 (and_29_out, pull_resistor_80_node, controlled_buffer_153_out);
  Pull_Resistor pull_resistor_95 (.node(controlled_buffer_153_out));
  and and_30 (and_30_out, pull_resistor_81_node, controlled_buffer_155_out);
  Pull_Resistor pull_resistor_96 (.node(controlled_buffer_155_out));
  and and_31 (and_31_out, pull_resistor_82_node, controlled_buffer_157_out);
  Pull_Resistor pull_resistor_97 (.node(controlled_buffer_157_out));
  and and_32 (and_32_out, pull_resistor_83_node, controlled_buffer_159_out);
  Pull_Resistor pull_resistor_98 (.node(controlled_buffer_159_out));
  or or_13 (or_13_out, pull_resistor_84_node, controlled_buffer_161_out);
  Pull_Resistor pull_resistor_99 (.node(controlled_buffer_161_out));
  or or_14 (or_14_out, pull_resistor_85_node, controlled_buffer_163_out);
  Pull_Resistor pull_resistor_100 (.node(controlled_buffer_163_out));
  or or_15 (or_15_out, pull_resistor_86_node, controlled_buffer_165_out);
  Pull_Resistor pull_resistor_101 (.node(controlled_buffer_165_out));
  or or_16 (or_16_out, pull_resistor_87_node, controlled_buffer_167_out);
  Pull_Resistor pull_resistor_102 (.node(controlled_buffer_167_out));
  xor xor_9 (xor_9_out, pull_resistor_88_node, controlled_buffer_169_out);
  Pull_Resistor pull_resistor_103 (.node(controlled_buffer_169_out));
  xor xor_10 (xor_10_out, pull_resistor_89_node, controlled_buffer_171_out);
  Pull_Resistor pull_resistor_104 (.node(controlled_buffer_171_out));
  xor xor_11 (xor_11_out, pull_resistor_90_node, controlled_buffer_173_out);
  Pull_Resistor pull_resistor_105 (.node(controlled_buffer_173_out));
  xor xor_12 (xor_12_out, pull_resistor_91_node, controlled_buffer_175_out);
  Pull_Resistor pull_resistor_106 (.node(controlled_buffer_175_out));
  D_Flip_Flop d_ff_45 (
    .D(controlled_buffer_176_out), .clk(controlled_buffer_179_out), .Q(d_ff_45_q), .Qn(d_ff_45_qn));  // open: preset, reset
  assign controlled_buffer_179_out = and_13_out ? and_15_out : 1'bz;  // Controlled_Buffer controlled_buffer_182
  not not_23 (not_23_out, pull_resistor_107_node);
  Pull_Resistor pull_resistor_107 (.node(pull_resistor_107_node));
  assign pull_resistor_107_node = not_20_out ? controlled_buffer_130_out : 1'bz;  // Controlled_Buffer controlled_buffer_183
  assign pull_resistor_72_node = decoder_6_out4 ? d_ff_44_q : 1'bz;  // Controlled_Buffer controlled_buffer_184
  assign controlled_buffer_88_out = decoder_6_out6 ? and_29_out : 1'bz;  // Controlled_Buffer controlled_buffer_185
  assign controlled_buffer_87_out = decoder_6_out6 ? and_30_out : 1'bz;  // Controlled_Buffer controlled_buffer_186
  assign controlled_buffer_86_out = decoder_6_out6 ? and_31_out : 1'bz;  // Controlled_Buffer controlled_buffer_187
  assign controlled_buffer_84_out = decoder_6_out6 ? and_32_out : 1'bz;  // Controlled_Buffer controlled_buffer_188
  assign controlled_buffer_88_out = decoder_6_out7 ? or_13_out : 1'bz;  // Controlled_Buffer controlled_buffer_189
  assign controlled_buffer_87_out = decoder_6_out7 ? or_14_out : 1'bz;  // Controlled_Buffer controlled_buffer_190
  assign controlled_buffer_86_out = decoder_6_out7 ? or_15_out : 1'bz;  // Controlled_Buffer controlled_buffer_191
  assign controlled_buffer_84_out = decoder_6_out7 ? or_16_out : 1'bz;  // Controlled_Buffer controlled_buffer_192
  assign controlled_buffer_88_out = decoder_6_out8 ? xor_9_out : 1'bz;  // Controlled_Buffer controlled_buffer_193
  assign controlled_buffer_87_out = decoder_6_out8 ? xor_10_out : 1'bz;  // Controlled_Buffer controlled_buffer_194
  assign controlled_buffer_86_out = decoder_6_out8 ? xor_11_out : 1'bz;  // Controlled_Buffer controlled_buffer_195
  assign controlled_buffer_84_out = decoder_6_out8 ? xor_12_out : 1'bz;  // Controlled_Buffer controlled_buffer_196
  not not_24 (not_24_out, d_ff_45_q);
  assign controlled_buffer_197_out = controlled_buffer_140_out ? not_24_out : 1'bz;  // Controlled_Buffer controlled_buffer_197
  assign controlled_buffer_84_out = and_16_out ? d_ff_45_q : 1'bz;  // Controlled_Buffer controlled_buffer_198
  assign controlled_buffer_199_out = and_19_out ? controlled_buffer_31_out : 1'bz;  // Controlled_Buffer controlled_buffer_199
  assign controlled_buffer_200_out = not_20_out ? not_23_out : 1'bz;  // Controlled_Buffer controlled_buffer_200
  D_Flip_Flop d_ff_46 (
    .D(controlled_buffer_199_out), .clk(controlled_buffer_151_out), .Q(d_ff_46_q));  // open: Qn, preset, reset
  Pull_Resistor pull_resistor_108 (.node(controlled_buffer_199_out));
  assign controlled_buffer_199_out = pull_resistor_107_node ? 1'b0 : 1'bz;  // Controlled_Buffer controlled_buffer_201
  assign controlled_buffer_84_out = or_7_out ? xor_5_out : 1'bz;  // Controlled_Buffer controlled_buffer_202
  assign controlled_buffer_86_out = or_7_out ? xor_6_out : 1'bz;  // Controlled_Buffer controlled_buffer_203
  assign controlled_buffer_87_out = or_7_out ? xor_7_out : 1'bz;  // Controlled_Buffer controlled_buffer_204
  assign controlled_buffer_88_out = or_7_out ? xor_8_out : 1'bz;  // Controlled_Buffer controlled_buffer_205
  assign controlled_buffer_206_out = and_13_out ? controlled_buffer_29_out : 1'bz;  // Controlled_Buffer controlled_buffer_206
  assign controlled_buffer_206_out = not_21_out ? d_ff_47_qn : 1'bz;  // Controlled_Buffer controlled_buffer_207
  assign controlled_buffer_197_out = not_17_out ? d_ff_45_q : 1'bz;  // Controlled_Buffer controlled_buffer_208
  Pull_Resistor pull_resistor_109 (.node(controlled_buffer_197_out));
  assign controlled_buffer_209_out = not_22_out ? controlled_buffer_197_out : 1'bz;  // Controlled_Buffer controlled_buffer_209
  assign controlled_buffer_210_out = and_19_out ? controlled_buffer_29_out : 1'bz;  // Controlled_Buffer controlled_buffer_210
  Pull_Resistor pull_resistor_110 (.node(controlled_buffer_210_out));
  assign controlled_buffer_210_out = pull_resistor_107_node ? d_ff_46_q : 1'bz;  // Controlled_Buffer controlled_buffer_211
  assign controlled_buffer_84_out = and_28_out ? d_ff_46_q : 1'bz;  // Controlled_Buffer controlled_buffer_212
  Pull_Resistor pull_resistor_111 (.node(or_7_out));
  D_Flip_Flop d_ff_47 (
    .D(controlled_buffer_206_out), .clk(controlled_buffer_209_out), .Q(d_ff_47_q), .Qn(d_ff_47_qn));  // open: preset, reset
  assign controlled_buffer_209_out = and_13_out ? and_15_out : 1'bz;  // Controlled_Buffer controlled_buffer_213
  assign controlled_buffer_199_out = controlled_buffer_200_out ? d_ff_48_q : 1'bz;  // Controlled_Buffer controlled_buffer_214
  D_Flip_Flop d_ff_48 (
    .D(controlled_buffer_210_out), .clk(controlled_buffer_151_out), .Q(d_ff_48_q));  // open: Qn, preset, reset
  assign controlled_buffer_86_out = and_28_out ? d_ff_48_q : 1'bz;  // Controlled_Buffer controlled_buffer_215
  not not_25 (not_25_out, d_ff_47_q);
  assign controlled_buffer_216_out = controlled_buffer_140_out ? not_25_out : 1'bz;  // Controlled_Buffer controlled_buffer_216
  assign controlled_buffer_86_out = and_16_out ? d_ff_47_q : 1'bz;  // Controlled_Buffer controlled_buffer_217
  assign controlled_buffer_218_out = and_19_out ? controlled_buffer_27_out : 1'bz;  // Controlled_Buffer controlled_buffer_218
  assign controlled_buffer_210_out = controlled_buffer_200_out ? d_ff_49_q : 1'bz;  // Controlled_Buffer controlled_buffer_219
  D_Flip_Flop d_ff_49 (
    .D(controlled_buffer_218_out), .clk(controlled_buffer_151_out), .Q(d_ff_49_q));  // open: Qn, preset, reset
  Pull_Resistor pull_resistor_112 (.node(controlled_buffer_218_out));
  assign controlled_buffer_218_out = pull_resistor_107_node ? d_ff_48_q : 1'bz;  // Controlled_Buffer controlled_buffer_220
  assign controlled_buffer_221_out = and_13_out ? controlled_buffer_27_out : 1'bz;  // Controlled_Buffer controlled_buffer_221
  assign controlled_buffer_221_out = not_21_out ? d_ff_50_qn : 1'bz;  // Controlled_Buffer controlled_buffer_222
  assign controlled_buffer_216_out = not_17_out ? d_ff_47_q : 1'bz;  // Controlled_Buffer controlled_buffer_223
  Pull_Resistor pull_resistor_113 (.node(controlled_buffer_216_out));
  assign controlled_buffer_224_out = not_22_out ? controlled_buffer_216_out : 1'bz;  // Controlled_Buffer controlled_buffer_224
  assign controlled_buffer_225_out = and_19_out ? controlled_buffer_25_out : 1'bz;  // Controlled_Buffer controlled_buffer_225
  Pull_Resistor pull_resistor_114 (.node(controlled_buffer_225_out));
  assign controlled_buffer_225_out = pull_resistor_107_node ? d_ff_49_q : 1'bz;  // Controlled_Buffer controlled_buffer_226
  Pull_Resistor pull_resistor_115 (.node(controlled_buffer_151_out));
  assign controlled_buffer_87_out = and_28_out ? d_ff_49_q : 1'bz;  // Controlled_Buffer controlled_buffer_227
  D_Flip_Flop d_ff_50 (
    .D(controlled_buffer_221_out), .clk(controlled_buffer_224_out), .Q(d_ff_50_q), .Qn(d_ff_50_qn));  // open: preset, reset
  assign controlled_buffer_224_out = and_13_out ? and_15_out : 1'bz;  // Controlled_Buffer controlled_buffer_228
  assign controlled_buffer_218_out = controlled_buffer_200_out ? d_ff_51_q : 1'bz;  // Controlled_Buffer controlled_buffer_229
  D_Flip_Flop d_ff_51 (
    .D(controlled_buffer_225_out), .clk(controlled_buffer_151_out), .Q(d_ff_51_q));  // open: Qn, preset, reset
  assign controlled_buffer_88_out = and_28_out ? d_ff_51_q : 1'bz;  // Controlled_Buffer controlled_buffer_230
  not not_26 (not_26_out, d_ff_50_q);
  assign controlled_buffer_231_out = controlled_buffer_140_out ? not_26_out : 1'bz;  // Controlled_Buffer controlled_buffer_231
  assign controlled_buffer_87_out = and_16_out ? d_ff_50_q : 1'bz;  // Controlled_Buffer controlled_buffer_232
  Pull_Resistor pull_resistor_116 (.node(controlled_buffer_200_out));
  assign controlled_buffer_225_out = controlled_buffer_200_out ? 1'b0 : 1'bz;  // Controlled_Buffer controlled_buffer_233
  assign controlled_buffer_234_out = and_13_out ? controlled_buffer_25_out : 1'bz;  // Controlled_Buffer controlled_buffer_234
  assign controlled_buffer_234_out = not_21_out ? d_ff_52_qn : 1'bz;  // Controlled_Buffer controlled_buffer_235
  assign controlled_buffer_231_out = not_17_out ? d_ff_50_q : 1'bz;  // Controlled_Buffer controlled_buffer_236
  Pull_Resistor pull_resistor_117 (.node(controlled_buffer_231_out));
  assign controlled_buffer_237_out = not_22_out ? controlled_buffer_231_out : 1'bz;  // Controlled_Buffer controlled_buffer_237
  D_Flip_Flop d_ff_52 (
    .D(controlled_buffer_234_out), .clk(controlled_buffer_237_out), .Q(d_ff_52_q), .Qn(d_ff_52_qn));  // open: preset, reset
  assign controlled_buffer_237_out = and_13_out ? and_15_out : 1'bz;  // Controlled_Buffer controlled_buffer_238
  assign controlled_buffer_88_out = and_16_out ? d_ff_52_q : 1'bz;  // Controlled_Buffer controlled_buffer_239
  Pull_Resistor pull_resistor_118 (.node(controlled_buffer_88_out));
  Pull_Resistor pull_resistor_119 (.node(controlled_buffer_87_out));
  Pull_Resistor pull_resistor_120 (.node(controlled_buffer_86_out));
  Pull_Resistor pull_resistor_121 (.node(controlled_buffer_84_out));

  // Notes on the sheet:
  //   contents of rom_1 (hex, n*v repeats v):
  //   0 0 0 51 c4 0 c8 0 c8 0 10 5*0 10*ff
endmodule
