// Logisim project ROMandCommandCounter.circ as structural Verilog: 1 circuit, main circuit main
module main (
);

  wire clock_1_out, clock_2_out, clock_3_out, controlled_buffer_1_out, controlled_buffer_3_out,
       controlled_buffer_5_out, controlled_buffer_7_out, controlled_buffer_8_out, controlled_buffer_11_out,
       controlled_buffer_13_out, controlled_buffer_15_out, controlled_buffer_17_out,
       controlled_buffer_19_out, controlled_buffer_21_out, controlled_buffer_23_out,
       controlled_buffer_25_out, controlled_buffer_27_out, controlled_buffer_29_out,
       controlled_buffer_31_out, controlled_buffer_33_out, d_ff_1_q, d_ff_1_qn, d_ff_2_qn, d_ff_3_qn,
       d_ff_4_qn, d_ff_5_qn, d_ff_6_qn, d_ff_7_qn, d_ff_8_qn, d_ff_9_qn, nand_1_out, pull_resistor_2_node;
  wire [7:0] d_ff_2_q, rom_1_data;

  assign controlled_buffer_1_out = d_ff_1_qn ? clock_1_out : 1'bz;  // Controlled_Buffer controlled_buffer_1
  Clock clock_1 (.out(clock_1_out));
  Clock #(.highDuration(3), .lowDuration(18)) clock_2 (.out(clock_2_out));
  Pull_Resistor pull_resistor_1 (.node(clock_2_out));
  D_Flip_Flop #(.trigger("falling")) d_ff_1 (
    .D(d_ff_1_qn), .clk(controlled_buffer_1_out), .Q(d_ff_1_q), .Qn(d_ff_1_qn), .reset(clock_2_out));  // open: preset
  nand nand_1 (nand_1_out, clock_2_out, 1'b1);
  Clock clock_3 (.out(clock_3_out));
  ROM rom_1 (.addr(d_ff_2_q), .data(rom_1_data));
  Pull_Resistor pull_resistor_2 (.node(pull_resistor_2_node));
  assign pull_resistor_2_node = d_ff_1_q ? clock_1_out : 1'bz;  // Controlled_Buffer controlled_buffer_2
  assign controlled_buffer_3_out = clock_2_out ? rom_1_data[0] : 1'bz;  // Controlled_Buffer controlled_buffer_3
  assign controlled_buffer_3_out = nand_1_out ? d_ff_2_qn : 1'bz;  // Controlled_Buffer controlled_buffer_4
  assign controlled_buffer_5_out = nand_1_out ? pull_resistor_2_node : 1'bz;  // Controlled_Buffer controlled_buffer_5
  assign controlled_buffer_5_out = clock_2_out ? clock_3_out : 1'bz;  // Controlled_Buffer controlled_buffer_6
  D_Flip_Flop #(.trigger("falling")) d_ff_2 (
    .D(controlled_buffer_3_out), .clk(controlled_buffer_5_out), .Q(d_ff_2_q[0]), .Qn(d_ff_2_qn));  // open: preset, reset
  assign controlled_buffer_7_out = nand_1_out ? d_ff_3_qn : 1'bz;  // Controlled_Buffer controlled_buffer_7
  assign controlled_buffer_8_out = nand_1_out ? d_ff_2_q[0] : 1'bz;  // Controlled_Buffer controlled_buffer_8
  assign controlled_buffer_8_out = clock_2_out ? controlled_buffer_5_out : 1'bz;  // Controlled_Buffer controlled_buffer_9
  assign controlled_buffer_7_out = clock_2_out ? rom_1_data[1] : 1'bz;  // Controlled_Buffer controlled_buffer_10
  D_Flip_Flop #(.trigger("falling")) d_ff_3 (
    .D(controlled_buffer_7_out), .clk(controlled_buffer_8_out), .Q(d_ff_2_q[1]), .Qn(d_ff_3_qn));  // open: preset, reset
  assign controlled_buffer_11_out = nand_1_out ? d_ff_4_qn : 1'bz;  // Controlled_Buffer controlled_buffer_11
  assign controlled_buffer_11_out = clock_2_out ? rom_1_data[2] : 1'bz;  // Controlled_Buffer controlled_buffer_12
  D_Flip_Flop #(.trigger("falling")) d_ff_4 (
    .D(controlled_buffer_11_out), .clk(controlled_buffer_13_out), .Q(d_ff_2_q[2]), .Qn(d_ff_4_qn));  // open: preset, reset
  assign controlled_buffer_13_out = nand_1_out ? d_ff_2_q[1] : 1'bz;  // Controlled_Buffer controlled_buffer_13
  assign controlled_buffer_13_out = clock_2_out ? controlled_buffer_8_out : 1'bz;  // Controlled_Buffer controlled_buffer_14
  assign controlled_buffer_15_out = clock_2_out ? rom_1_data[3] : 1'bz;  // Controlled_Buffer controlled_buffer_15
  assign controlled_buffer_15_out = nand_1_out ? d_ff_5_qn : 1'bz;  // Controlled_Buffer controlled_buffer_16
  assign controlled_buffer_17_out = nand_1_out ? d_ff_2_q[2] : 1'bz;  // Controlled_Buffer controlled_buffer_17
  assign controlled_buffer_17_out = clock_2_out ? controlled_buffer_13_out : 1'bz;  // Controlled_Buffer controlled_buffer_18
  D_Flip_Flop #(.trigger("falling")) d_ff_5 (
    .D(controlled_buffer_15_out), .clk(controlled_buffer_17_out), .Q(d_ff_2_q[3]), .Qn(d_ff_5_qn));  // open: preset, reset
  assign controlled_buffer_19_out = nand_1_out ? d_ff_6_qn : 1'bz;  // Controlled_Buffer controlled_buffer_19
  assign controlled_buffer_19_out = clock_2_out ? rom_1_data[4] : 1'bz;  // Controlled_Buffer controlled_buffer_20
  D_Flip_Flop #(.trigger("falling")) d_ff_6 (
    .D(controlled_buffer_19_out), .clk(controlled_buffer_21_out), .Q(d_ff_2_q[4]), .Qn(d_ff_6_qn));  // open: preset, reset
  assign controlled_buffer_21_out = nand_1_out ? d_ff_2_q[3] : 1'bz;  // Controlled_Buffer controlled_buffer_21
  assign controlled_buffer_21_out = clock_2_out ? controlled_buffer_17_out : 1'bz;  // Controlled_Buffer controlled_buffer_22
  assign controlled_buffer_23_out = clock_2_out ? rom_1_data[5] : 1'bz;  // Controlled_Buffer controlled_buffer_23
  assign controlled_buffer_23_out = nand_1_out ? d_ff_7_qn : 1'bz;  // Controlled_Buffer controlled_buffer_24
  assign controlled_buffer_25_out = nand_1_out ? d_ff_2_q[4] : 1'bz;  // Controlled_Buffer controlled_buffer_25
  assign controlled_buffer_25_out = clock_2_out ? controlled_buffer_21_out : 1'bz;  // Controlled_Buffer controlled_buffer_26
  D_Flip_Flop #(.trigger("falling")) d_ff_7 (
    .D(controlled_buffer_23_out), .clk(controlled_buffer_25_out), .Q(d_ff_2_q[5]), .Qn(d_ff_7_qn));  // open: preset, reset
  assign controlled_buffer_27_out = clock_2_out ? rom_1_data[6] : 1'bz;  // Controlled_Buffer controlled_buffer_27
  assign controlled_buffer_27_out = nand_1_out ? d_ff_8_qn : 1'bz;  // Controlled_Buffer controlled_buffer_28
  assign controlled_buffer_29_out = nand_1_out ? d_ff_2_q[5] : 1'bz;  // Controlled_Buffer controlled_buffer_29
  assign controlled_buffer_29_out = clock_2_out ? controlled_buffer_25_out : 1'bz;  // Controlled_Buffer controlled_buffer_30
  D_Flip_Flop #(.trigger("falling")) d_ff_8 (
    .D(controlled_buffer_27_out), .clk(controlled_buffer_29_out), .Q(d_ff_2_q[6]), .Qn(d_ff_8_qn));  // open: preset, reset
  assign controlled_buffer_31_out = nand_1_out ? d_ff_9_qn : 1'bz;  // Controlled_Buffer controlled_buffer_31
  assign controlled_buffer_31_out = clock_2_out ? rom_1_data[7] : 1'bz;  // Controlled_Buffer controlled_buffer_32
  D_Flip_Flop #(.trigger("falling")) d_ff_9 (
    .D(controlled_buffer_31_out), .clk(controlled_buffer_33_out), .Q(d_ff_2_q[7]), .Qn(d_ff_9_qn));  // open: preset, reset
  assign controlled_buffer_33_out = nand_1_out ? d_ff_2_q[6] : 1'bz;  // Controlled_Buffer controlled_buffer_33
  assign controlled_buffer_33_out = clock_2_out ? controlled_buffer_29_out : 1'bz;  // Controlled_Buffer controlled_buffer_34

  // Notes on the sheet:
  //   contents of rom_1 (hex, n*v repeats v):
  //   11 22 33 44 55 66 77 88 99 0 10 5*0 10*ff
endmodule
