// Logisim project Registers.circ as structural Verilog: 1 circuit, main circuit main
module main (
);

  wire clock_1_out, controlled_buffer_1_out, controlled_buffer_2_out, controlled_buffer_3_out,
       controlled_buffer_4_out, controlled_buffer_5_out, controlled_buffer_6_out, controlled_buffer_7_out,
       controlled_buffer_8_out, controlled_buffer_9_out, controlled_buffer_10_out, controlled_buffer_11_out,
       controlled_buffer_12_out, controlled_buffer_13_out, controlled_buffer_14_out,
       controlled_buffer_15_out, controlled_buffer_16_out, controlled_buffer_17_out,
       controlled_buffer_18_out, controlled_buffer_19_out, controlled_buffer_20_out,
       controlled_buffer_21_out, controlled_buffer_22_out, controlled_buffer_23_out,
       controlled_buffer_24_out, controlled_buffer_25_out, controlled_buffer_26_out,
       controlled_buffer_27_out, controlled_buffer_28_out, d_ff_1_q, d_ff_2_q, d_ff_3_q, d_ff_4_q, d_ff_5_q,
       d_ff_6_q, d_ff_7_q, d_ff_8_q, d_ff_9_q, d_ff_10_q, d_ff_11_q, d_ff_12_q, d_ff_13_q, d_ff_14_q,
       d_ff_15_q, d_ff_16_q, decoder_1_out0, decoder_1_out1, decoder_1_out2, decoder_1_out3, decoder_2_out0,
       decoder_2_out1, decoder_2_out2, decoder_2_out3, decoder_3_out0, decoder_3_out1, decoder_3_out2,
       decoder_3_out3, dipswitch_1_sw1, dipswitch_1_sw2, dipswitch_1_sw3, dipswitch_1_sw4;
  wire [1:0] dipswitch_2_sw1, dipswitch_2_sw5, dipswitch_2_sw7;

  DipSwitch dipswitch_1 (
    .sw1(dipswitch_1_sw1), .sw2(dipswitch_1_sw2), .sw3(dipswitch_1_sw3), .sw4(dipswitch_1_sw4));  // open: sw5, sw6, sw7, sw8
  Decoder #(.select(2)) decoder_1 (
    .out0(decoder_1_out0), .out1(decoder_1_out1), .out2(decoder_1_out2), .out3(decoder_1_out3),
    .sel(dipswitch_2_sw1));  // open: en
  LED led_1 (.in(clock_1_out));
  Clock clock_1 (.out(clock_1_out));
  DipSwitch dipswitch_2 (
    .sw1(dipswitch_2_sw1[0]), .sw2(dipswitch_2_sw1[1]), .sw5(dipswitch_2_sw5[0]), .sw6(dipswitch_2_sw5[1]),
    .sw7(dipswitch_2_sw7[0]), .sw8(dipswitch_2_sw7[1]));  // open: sw3, sw4
  assign controlled_buffer_1_out = decoder_1_out0 ? dipswitch_1_sw1 : 1'bz;  // Controlled_Buffer controlled_buffer_1
  assign controlled_buffer_2_out = decoder_1_out0 ? clock_1_out : 1'bz;  // Controlled_Buffer controlled_buffer_2
  assign controlled_buffer_3_out = decoder_1_out0 ? dipswitch_1_sw2 : 1'bz;  // Controlled_Buffer controlled_buffer_3
  assign controlled_buffer_4_out = decoder_1_out0 ? dipswitch_1_sw3 : 1'bz;  // Controlled_Buffer controlled_buffer_4
  assign controlled_buffer_5_out = decoder_1_out0 ? dipswitch_1_sw4 : 1'bz;  // Controlled_Buffer controlled_buffer_5
  assign controlled_buffer_6_out = decoder_1_out1 ? dipswitch_1_sw1 : 1'bz;  // Controlled_Buffer controlled_buffer_6
  assign controlled_buffer_7_out = decoder_1_out1 ? clock_1_out : 1'bz;  // Controlled_Buffer controlled_buffer_7
  assign controlled_buffer_8_out = decoder_1_out1 ? dipswitch_1_sw2 : 1'bz;  // Controlled_Buffer controlled_buffer_8
  assign controlled_buffer_9_out = decoder_1_out1 ? dipswitch_1_sw3 : 1'bz;  // Controlled_Buffer controlled_buffer_9
  assign controlled_buffer_10_out = decoder_1_out1 ? dipswitch_1_sw4 : 1'bz;  // Controlled_Buffer controlled_buffer_10
  assign controlled_buffer_11_out = decoder_1_out2 ? dipswitch_1_sw1 : 1'bz;  // Controlled_Buffer controlled_buffer_11
  assign controlled_buffer_12_out = decoder_1_out2 ? clock_1_out : 1'bz;  // Controlled_Buffer controlled_buffer_12
  assign controlled_buffer_13_out = decoder_1_out2 ? dipswitch_1_sw2 : 1'bz;  // Controlled_Buffer controlled_buffer_13
  assign controlled_buffer_14_out = decoder_1_out2 ? dipswitch_1_sw3 : 1'bz;  // Controlled_Buffer controlled_buffer_14
  assign controlled_buffer_15_out = decoder_1_out2 ? dipswitch_1_sw4 : 1'bz;  // Controlled_Buffer controlled_buffer_15
  assign controlled_buffer_16_out = decoder_1_out3 ? dipswitch_1_sw1 : 1'bz;  // Controlled_Buffer controlled_buffer_16
  assign controlled_buffer_17_out = decoder_1_out3 ? clock_1_out : 1'bz;  // Controlled_Buffer controlled_buffer_17
  assign controlled_buffer_18_out = decoder_1_out3 ? dipswitch_1_sw2 : 1'bz;  // Controlled_Buffer controlled_buffer_18
  assign controlled_buffer_19_out = decoder_1_out3 ? dipswitch_1_sw3 : 1'bz;  // Controlled_Buffer controlled_buffer_19
  assign controlled_buffer_20_out = decoder_1_out3 ? dipswitch_1_sw4 : 1'bz;  // Controlled_Buffer controlled_buffer_20
  D_Flip_Flop d_ff_1 (
    .D(controlled_buffer_1_out), .clk(controlled_buffer_2_out), .Q(d_ff_1_q));  // open: Qn, preset, reset
  D_Flip_Flop d_ff_2 (
    .D(controlled_buffer_3_out), .clk(controlled_buffer_2_out), .Q(d_ff_2_q));  // open: Qn, preset, reset
  D_Flip_Flop d_ff_3 (
    .D(controlled_buffer_4_out), .clk(controlled_buffer_2_out), .Q(d_ff_3_q));  // open: Qn, preset, reset
  D_Flip_Flop d_ff_4 (
    .D(controlled_buffer_5_out), .clk(controlled_buffer_2_out), .Q(d_ff_4_q));  // open: Qn, preset, reset
  Pull_Resistor pull_resistor_1 (.node(controlled_buffer_2_out));
  D_Flip_Flop d_ff_5 (
    .D(controlled_buffer_6_out), .clk(controlled_buffer_7_out), .Q(d_ff_5_q));  // open: Qn, preset, reset
  D_Flip_Flop d_ff_6 (
    .D(controlled_buffer_8_out), .clk(controlled_buffer_7_out), .Q(d_ff_6_q));  // open: Qn, preset, reset
  D_Flip_Flop d_ff_7 (
    .D(controlled_buffer_9_out), .clk(controlled_buffer_7_out), .Q(d_ff_7_q));  // open: Qn, preset, reset
  D_Flip_Flop d_ff_8 (
    .D(controlled_buffer_10_out), .clk(controlled_buffer_7_out), .Q(d_ff_8_q));  // open: Qn, preset, reset
  Pull_Resistor pull_resistor_2 (.node(controlled_buffer_7_out));
  D_Flip_Flop d_ff_9 (
    .D(controlled_buffer_11_out), .clk(controlled_buffer_12_out), .Q(d_ff_9_q));  // open: Qn, preset, reset
  D_Flip_Flop d_ff_10 (
    .D(controlled_buffer_13_out), .clk(controlled_buffer_12_out), .Q(d_ff_10_q));  // open: Qn, preset, reset
  D_Flip_Flop d_ff_11 (
    .D(controlled_buffer_14_out), .clk(controlled_buffer_12_out), .Q(d_ff_11_q));  // open: Qn, preset, reset
  D_Flip_Flop d_ff_12 (
    .D(controlled_buffer_15_out), .clk(controlled_buffer_12_out), .Q(d_ff_12_q));  // open: Qn, preset, reset
  Pull_Resistor pull_resistor_3 (.node(controlled_buffer_12_out));
  D_Flip_Flop d_ff_13 (
    .D(controlled_buffer_16_out), .clk(controlled_buffer_17_out), .Q(d_ff_13_q));  // open: Qn, preset, reset
  D_Flip_Flop d_ff_14 (
    .D(controlled_buffer_18_out), .clk(controlled_buffer_17_out), .Q(d_ff_14_q));  // open: Qn, preset, reset
  D_Flip_Flop d_ff_15 (
    .D(controlled_buffer_19_out), .clk(controlled_buffer_17_out), .Q(d_ff_15_q));  // open: Qn, preset, reset
  D_Flip_Flop d_ff_16 (
    .D(controlled_buffer_20_out), .clk(controlled_buffer_17_out), .Q(d_ff_16_q));  // open: Qn, preset, reset
  Pull_Resistor pull_resistor_4 (.node(controlled_buffer_17_out));
  assign controlled_buffer_21_out = decoder_2_out0 ? d_ff_1_q : 1'bz;  // Controlled_Buffer controlled_buffer_21
  assign controlled_buffer_22_out = decoder_3_out0 ? d_ff_1_q : 1'bz;  // Controlled_Buffer controlled_buffer_22
  assign controlled_buffer_23_out = decoder_2_out0 ? d_ff_2_q : 1'bz;  // Controlled_Buffer controlled_buffer_23
  assign controlled_buffer_24_out = decoder_3_out0 ? d_ff_2_q : 1'bz;  // Controlled_Buffer controlled_buffer_24
  assign controlled_buffer_25_out = decoder_2_out0 ? d_ff_3_q : 1'bz;  // Controlled_Buffer controlled_buffer_25
  assign controlled_buffer_26_out = decoder_3_out0 ? d_ff_3_q : 1'bz;  // Controlled_Buffer controlled_buffer_26
  assign controlled_buffer_27_out = decoder_2_out0 ? d_ff_4_q : 1'bz;  // Controlled_Buffer controlled_buffer_27
  assign controlled_buffer_28_out = decoder_3_out0 ? d_ff_4_q : 1'bz;  // Controlled_Buffer controlled_buffer_28
  assign controlled_buffer_21_out = decoder_2_out1 ? d_ff_5_q : 1'bz;  // Controlled_Buffer controlled_buffer_29
  assign controlled_buffer_22_out = decoder_3_out1 ? d_ff_5_q : 1'bz;  // Controlled_Buffer controlled_buffer_30
  assign controlled_buffer_23_out = decoder_2_out1 ? d_ff_6_q : 1'bz;  // Controlled_Buffer controlled_buffer_31
  assign controlled_buffer_24_out = decoder_3_out1 ? d_ff_6_q : 1'bz;  // Controlled_Buffer controlled_buffer_32
  assign controlled_buffer_25_out = decoder_2_out1 ? d_ff_7_q : 1'bz;  // Controlled_Buffer controlled_buffer_33
  assign controlled_buffer_26_out = decoder_3_out1 ? d_ff_7_q : 1'bz;  // Controlled_Buffer controlled_buffer_34
  assign controlled_buffer_27_out = decoder_2_out1 ? d_ff_8_q : 1'bz;  // Controlled_Buffer controlled_buffer_35
  assign controlled_buffer_28_out = decoder_3_out1 ? d_ff_8_q : 1'bz;  // Controlled_Buffer controlled_buffer_36
  assign controlled_buffer_21_out = decoder_2_out2 ? d_ff_9_q : 1'bz;  // Controlled_Buffer controlled_buffer_37
  assign controlled_buffer_22_out = decoder_3_out2 ? d_ff_9_q : 1'bz;  // Controlled_Buffer controlled_buffer_38
  assign controlled_buffer_23_out = decoder_2_out2 ? d_ff_10_q : 1'bz;  // Controlled_Buffer controlled_buffer_39
  assign controlled_buffer_24_out = decoder_3_out2 ? d_ff_10_q : 1'bz;  // Controlled_Buffer controlled_buffer_40
  assign controlled_buffer_25_out = decoder_2_out2 ? d_ff_11_q : 1'bz;  // Controlled_Buffer controlled_buffer_41
  assign controlled_buffer_26_out = decoder_3_out2 ? d_ff_11_q : 1'bz;  // Controlled_Buffer controlled_buffer_42
  assign controlled_buffer_27_out = decoder_2_out2 ? d_ff_12_q : 1'bz;  // Controlled_Buffer controlled_buffer_43
  assign controlled_buffer_28_out = decoder_3_out2 ? d_ff_12_q : 1'bz;  // Controlled_Buffer controlled_buffer_44
  assign controlled_buffer_21_out = decoder_2_out3 ? d_ff_13_q : 1'bz;  // Controlled_Buffer controlled_buffer_45
  assign controlled_buffer_22_out = decoder_3_out3 ? d_ff_13_q : 1'bz;  // Controlled_Buffer controlled_buffer_46
  assign controlled_buffer_23_out = decoder_2_out3 ? d_ff_14_q : 1'bz;  // Controlled_Buffer controlled_buffer_47
  assign controlled_buffer_24_out = decoder_3_out3 ? d_ff_14_q : 1'bz;  // Controlled_Buffer controlled_buffer_48
  assign controlled_buffer_25_out = decoder_2_out3 ? d_ff_15_q : 1'bz;  // Controlled_Buffer controlled_buffer_49
  assign controlled_buffer_26_out = decoder_3_out3 ? d_ff_15_q : 1'bz;  // Controlled_Buffer controlled_buffer_50
  assign controlled_buffer_27_out = decoder_2_out3 ? d_ff_16_q : 1'bz;  // Controlled_Buffer controlled_buffer_51
  assign controlled_buffer_28_out = decoder_3_out3 ? d_ff_16_q : 1'bz;  // Controlled_Buffer controlled_buffer_52
  Decoder #(.select(2)) decoder_2 (
    .out0(decoder_2_out0), .out1(decoder_2_out1), .out2(decoder_2_out2), .out3(decoder_2_out3),
    .sel(dipswitch_2_sw5));  // open: en
  Decoder #(.select(2)) decoder_3 (
    .out0(decoder_3_out0), .out1(decoder_3_out1), .out2(decoder_3_out2), .out3(decoder_3_out3),
    .sel(dipswitch_2_sw7));  // open: en
  LED led_2 (.in(controlled_buffer_21_out));
  LED led_3 (.in(controlled_buffer_23_out));
  LED led_4 (.in(controlled_buffer_25_out));
  LED led_5 (.in(controlled_buffer_27_out));
  LED led_6 (.in(controlled_buffer_22_out));
  LED led_7 (.in(controlled_buffer_24_out));
  LED led_8 (.in(controlled_buffer_26_out));
  LED led_9 (.in(controlled_buffer_28_out));
endmodule
